# Fritzing sketch esquematico (saved by Fritzing 0.9.3b)
circuit board: 8.46667cm x 5.64444cm
breadboards: 1

parts:
  Raspberry_Pi1 = Raspberry Pi 2
  Alimentaçao = female pin header, 2 pins [form="♀ (female)"]
  motor_esq = female pin header, 2 pins [form="♀ (female)"]
  sensor_linha_esq = female pin header, 3 pins [form="♀ (female)"]
  sensor_linha_cen = female pin header, 3 pins [form="♀ (female)"]
  sensor_linha_dir = female pin header, 3 pins [form="♀ (female)"]
  motor_dir = female pin header, 2 pins [form="♀ (female)"]
  servo = female pin header, 3 pins [form="♀ (female)"]
  us = female pin header, 4 pins [form="♀ (female)"]
  12V_-_motor = female pin header, 3 pins [form="♀ (female)"]
  J1 = female pin header, 20 pins [form="♀ (female)"]  # not connected
  J2 = female pin header, 20 pins [form="♀ (female)"]  # not connected
  330 = Resistor [tolerance=±5% resistance=330 package=THT]
  470 = Resistor [tolerance=±5% resistance=470 package=THT]
  switch = female pin header, 3 pins [form="♀ (female)"]
  J3 = female pin header, 1 pin [form="♀ (female)"]  # not connected

nets (from the schematic view):
  N1: Raspberry_Pi1.GPIO17, motor_dir.pin2
  N2: Raspberry_Pi1.GPIO22, motor_esq.pin2
  N3: Raspberry_Pi1.GPIO11, sensor_linha_esq.pin3
  N4: Raspberry_Pi1.GND, Alimentaçao.pin2, sensor_linha_esq.pin2, sensor_linha_cen.pin2, sensor_linha_dir.pin2, servo.pin2, us.pin4, 12V_-_motor.pin3, 470.Pin_1
  N5: Raspberry_Pi1.GPIO13, us.pin2
  N6: Raspberry_Pi1.GPIO19, servo.pin3
  N7: Raspberry_Pi1.GPIO26, sensor_linha_cen.pin3
  N8: Raspberry_Pi1.GPIO16, 330.Pin_0, 470.Pin_0
  N9: Raspberry_Pi1.GPIO12, sensor_linha_dir.pin3
  N10: Raspberry_Pi1.GPIO23, motor_esq.pin1
  N11: Raspberry_Pi1.GPIO18, motor_dir.pin1
  N12: Raspberry_Pi1.5V, Alimentaçao.pin1
  N13: sensor_linha_esq.pin1, sensor_linha_cen.pin1, sensor_linha_dir.pin1, servo.pin1, us.pin1
  N14: us.pin3, 330.Pin_1
  N15: 12V_-_motor.pin1, switch.pin3
  N16: 12V_-_motor.pin2, switch.pin2
